// Logisim project CPU R4-D4.circ as structural Verilog: 5 circuits, main circuit Banco de registradores
module Banco_de_registradores (
  input  Clear,
  input  clock,
  input  [7:0] Dado_a_ser_escrito,
  input  escrever_REG,
  input  [1:0] REG_1,
  input  [1:0] REG_2,
  output [7:0] REG_1_LIDO,
  output [7:0] REG_00,
  output [7:0] REG_2_LIDO,
  output [7:0] REG_01,
  output [7:0] REG_10,
  output [7:0] REG_11
);

  wire demultiplexer_1_out0, demultiplexer_1_out1, demultiplexer_1_out2, demultiplexer_1_out3;

  Demultiplexer #(.select(2), .enable("false")) demultiplexer_1 (
    .out0(demultiplexer_1_out0), .out1(demultiplexer_1_out1), .out2(demultiplexer_1_out2),
    .out3(demultiplexer_1_out3), .in(escrever_REG), .sel(REG_1));
  Register register_1 (.D(Dado_a_ser_escrito), .en(demultiplexer_1_out0), .Q(REG_00), .clk(clock), .clr(Clear));
  Register register_2 (.D(Dado_a_ser_escrito), .en(demultiplexer_1_out1), .Q(REG_01), .clk(clock), .clr(Clear));
  Register register_3 (.D(Dado_a_ser_escrito), .en(demultiplexer_1_out2), .Q(REG_10), .clk(clock), .clr(Clear));
  Register register_4 (.D(Dado_a_ser_escrito), .en(demultiplexer_1_out3), .Q(REG_11), .clk(clock), .clr(Clear));
  Multiplexer #(.select(2), .width(8), .enable("false")) multiplexer_1 (
    .in0(REG_00), .in1(REG_01), .in2(REG_10), .in3(REG_11), .out(REG_1_LIDO), .sel(REG_1));
  Multiplexer #(.select(2), .width(8), .enable("false")) multiplexer_2 (
    .in0(REG_00), .in1(REG_01), .in2(REG_10), .in3(REG_11), .out(REG_2_LIDO), .sel(REG_2));
endmodule

module Unidade_de_controle (
  input  [3:0] _0000_ADD,
  output \Endereço ,
  output Jump,
  output Branch,
  output [1:0] MemtoReg,
  output [2:0] ALUOP,
  output MemWrite_MemRead,
  output ALUSrc,
  output RegWrite
);

  Multiplexer #(.select(4), .width(11), .enable("false")) multiplexer_1 (
    .in0(11'h408), .in1(11'h608), .in2(11'h428), .in3(11'h628), .in4(11'h24), .in5(11'h2), .in6(11'h101),
    .in7(11'h411), .in8(11'h448), .in9(11'h468), .in10(11'h488), .in11(11'h4a8), .in12(11'h4c8),
    .in13(11'h4e8), .out({RegWrite, ALUSrc, MemWrite_MemRead, ALUOP, MemtoReg, Branch, Jump, \Endereço }),
    .sel(_0000_ADD));  // open: in14, in15

  // Notes on the sheet:
  //   0001 ADDI
  //   0010 SUB
  //   0011 SUBi
  //   0100 BEQ
  //   0101 JUMP
  //   0110 SW
  //   0111 LW
  //   1000 AND
  //   1001 NAND
  //   1010 OR
  //   1011 NOR
  //   1100 XOR
  //   1101 NOT
  //   0100 BEQ
  //   0011 SUBi
  //   0010 SUB
  //   0001 ADDI
  //   0000 ADD
  //   1101 NOT
  //   1100 XOR
  //   1011 NOR
  //   1010 OR
  //   1001 NAND
  //   1000 AND
  //   0111 LW
  //   0110 SW
  //   0101 JUMP
endmodule

module \Memória_de_dados  (
  input  [7:0] dado_a_ser_escrito,
  input  [7:0] seletor,
  input  Enable_do_seletor,
  input  load,
  input  clear,
  input  clock,
  output [7:0] dado_lido
);

  wire not_1_out;

  assign dado_lido = not_1_out ? dado_a_ser_escrito : 8'bz;  // Controlled_Buffer controlled_buffer_1
  not not_1 (not_1_out, load);
  RAM ram_1 (.addr(seletor), .data(dado_lido), .sel(Enable_do_seletor), .clk(clock), .ld(load), .clr(clear));
endmodule

module ALU (
  input  [2:0] OP_ULA,
  input  [7:0] entrada_A,
  input  [7:0] entrada_B,
  output overflow,
  output zero,
  output [7:0] \saída 
);

  wire adder_1_cout, subtractor_1_bout;
  wire [7:0] adder_1_out, and_1_out, not_1_out, not_2_out, not_3_out, or_2_out, subtractor_1_out, xor_1_out;

  or or_1 (overflow, subtractor_1_bout, adder_1_cout);
  Adder adder_1 (.a(entrada_A), .b(entrada_B), .out(adder_1_out), .cout(adder_1_cout));  // open: cin
  Subtractor subtractor_1 (
    .a(entrada_A), .b(entrada_B), .out(subtractor_1_out), .bout(subtractor_1_bout));  // open: bin
  assign not_1_out = ~entrada_A;  // NOT_Gate not_1, 8 bits wide
  assign and_1_out = entrada_A & entrada_B;  // AND_Gate and_1, 8 bits wide
  assign not_2_out = ~and_1_out;  // NOT_Gate not_2, 8 bits wide
  assign or_2_out = entrada_A | entrada_B;  // OR_Gate or_2, 8 bits wide
  assign not_3_out = ~or_2_out;  // NOT_Gate not_3, 8 bits wide
  assign xor_1_out = entrada_A ^ entrada_B;  // XOR_Gate xor_1, 8 bits wide
  Comparator comparator_1 (.a(subtractor_1_out), .b({8{1'b0}}), .eq(zero));  // open: gt, lt
  Multiplexer #(.select(3), .width(8), .enable("false")) multiplexer_1 (
    .in0(adder_1_out), .in1(subtractor_1_out), .in2(and_1_out), .in3(not_2_out), .in4(or_2_out),
    .in5(not_3_out), .in6(xor_1_out), .in7(not_1_out), .out(\saída ), .sel(OP_ULA));
endmodule

module cpu_organizada (
  input  in_1,
  output [7:0] REG_00,
  output [7:0] REG_01,
  output [7:0] REG_10,
  output [7:0] REG_11,
  output [7:0] ULA_A,
  output [7:0] ULA_B,
  output [7:0] ULA_S,
  output [2:0] ULAOp,
  output [7:0] \Endereço_Instrução ,
  output [3:0] OP_cpu,
  output [1:0] R2,
  output [1:0] R1,
  output [7:0] Input,
  output [7:0] out_15
);

  wire alu_1_overflow, alu_1_zero, and_1_out, and_2_out, clear_2_out, clear_3_out, clear_4_out, clear_out,
       CLOCK, not_1_out, not_2_out, not_3_out, unidade_de_controle_1_alusrc, unidade_de_controle_1_branch,
       \unidade_de_controle_1_endereço , unidade_de_controle_1_jump, unidade_de_controle_1_memwrite_memread,
       unidade_de_controle_1_regwrite;
  wire [1:0] unidade_de_controle_1_memtoreg;
  wire [7:0] banco_de_registradores_1_reg_2_lido, \memória_de_dados_1_dado_lido , multiplexer_1_out,
       multiplexer_3_out;

  Clock clock_1 (.out(CLOCK));
  not not_1 (not_1_out, and_1_out);
  Counter counter_1 (
    .load(not_1_out), .D(Input), .count(and_1_out), .Q(\Endereço_Instrução ), .clk(CLOCK), .clr(clear_out));  // open: carry
  Button clear (.out(clear_out));
  Button clear_2 (.out(clear_2_out));
  RAM #(.dataWidth(16)) ram_1 (
    .addr(\Endereço_Instrução ), .data({OP_cpu, R2, R1, Input}), .clk(CLOCK), .clr(clear_2_out));  // open: sel, ld
  Multiplexer #(.select(2), .width(8), .enable("false")) multiplexer_1 (
    .in0(Input), .in1(out_15), .in2(\memória_de_dados_1_dado_lido ), .out(multiplexer_1_out),
    .sel(unidade_de_controle_1_memtoreg));  // open: in3
  and and_1 (and_1_out, not_3_out, not_2_out);
  not not_2 (not_2_out, unidade_de_controle_1_jump);
  Unidade_de_controle unidade_de_controle_1 (
    ._0000_ADD(OP_cpu), .Jump(unidade_de_controle_1_jump), .Branch(unidade_de_controle_1_branch),
    .ALUOP(ULAOp), .MemWrite_MemRead(unidade_de_controle_1_memwrite_memread),
    .ALUSrc(unidade_de_controle_1_alusrc), .RegWrite(unidade_de_controle_1_regwrite),
    .MemtoReg(unidade_de_controle_1_memtoreg), .\Endereço (\unidade_de_controle_1_endereço ));
  Button clear_3 (.out(clear_3_out));
  Banco_de_registradores banco_de_registradores_1 (
    .Dado_a_ser_escrito(multiplexer_1_out), .REG_1_LIDO(ULA_A),
    .REG_2_LIDO(banco_de_registradores_1_reg_2_lido), .Clear(clear_3_out), .REG_1(R1), .REG_2(R2),
    .clock(CLOCK), .escrever_REG(unidade_de_controle_1_regwrite), .REG_00(REG_00), .REG_01(REG_01),
    .REG_10(REG_10), .REG_11(REG_11));
  not not_3 (not_3_out, and_2_out);
  Multiplexer #(.width(8), .enable("false")) multiplexer_2 (
    .in0(banco_de_registradores_1_reg_2_lido), .in1(Input), .out(ULA_B), .sel(unidade_de_controle_1_alusrc));
  and and_2 (and_2_out, unidade_de_controle_1_branch, alu_1_zero);
  ALU alu_1 (
    .entrada_A(ULA_A), .entrada_B(ULA_B), .\saída (out_15), .overflow(alu_1_overflow), .zero(alu_1_zero),
    .OP_ULA(ULAOp));
  LED led_1 (.in(alu_1_overflow));
  Multiplexer #(.width(8), .enable("false")) multiplexer_3 (
    .in0(out_15), .in1(Input), .out(multiplexer_3_out), .sel(\unidade_de_controle_1_endereço ));
  \Memória_de_dados  \memória_de_dados_1  (
    .dado_lido(\memória_de_dados_1_dado_lido ), .dado_a_ser_escrito(banco_de_registradores_1_reg_2_lido),
    .seletor(multiplexer_3_out), .Enable_do_seletor(unidade_de_controle_1_memwrite_memread), .load(in_1),
    .clear(clear_4_out), .clock(CLOCK));
  Button clear_4 (.out(clear_4_out));

  assign ULA_S = out_15;

  // Other names for the same wires on the sheet: a[7:0] = ULA_A; b[7:0] = ULA_B; end_inst[7:0] = \Endereço_Instrução ;
  //   op_inst[3:0] = OP_cpu; reg_1[1:0] = R1; reg_2[1:0] = R2; s[7:0] = out_15

  // Notes on the sheet:
  //   000 ADD
  //   001 SUB
  //   010 AND
  //   011 NAND
  //   100 OR
  //   101 NOR
  //   110 XOR
  //   111 NOT
  //   0000 ADD
  //   0001 ADDI
  //   0010 SUB
  //   0011 SUBi
  //   0100 BEQ
  //   0101 JUMP
  //   0110 SW
  //   0111 LW
  //   1000 AND
  //   1001 NAND
  //   1010 OR
  //   1011 NOR
  //   1100 XOR
  //   1101 NOT
  //   Jump
  //   Branch
  //   endereço
  //   MemtoReg
  //   ALUOp
  //   MEM read/write
  //   ALUSrc
  //   RegWrite
endmodule
